# Fritzing sketch wiring diagram design2 (saved by Fritzing 0.9.5d)
breadboards: 2

parts:
  A1 = HC-SR04 Ultrasonic Distance Sensor
  A2 = HC-SR04 Ultrasonic Distance Sensor
  L298N1 = L298N DC motor driver
  DC_Mot_Enc1 = DC Motor with two-phase hall-encoder [part_number=VT-E-G25A-06-177E]
  DC_Mot_Enc2 = DC Motor with two-phase hall-encoder [part_number=VT-E-G25A-06-177E]
  Load_Cell1 = Load Cell - Red/white/black/green
  Load_Cell2 = Load Cell - Red/white/black/green
  A3 = Raspberry Pi 5
  U1 = ESP32-38PinWide [part_number=ESP32-38PinWide]
  J1 = Basic Servo
  J2 = Basic Servo
  S1 = Round Pushbutton
  BAT3 = 12 battery [package=battery]
  M1 = RioRand LM2596
  M2 = RioRand LM2596
  M3 = RioRand LM2596
  A4 = Sparkfun load cell amplifier
  A5 = Sparkfun load cell amplifier
  S2 = Round Pushbutton
  A6 = BBAA100043

nets:
  VCC: A1.VCC, A2.VCC, M1.Pin_3, A4.Pin_9, A5.Pin_9
  N1: A1.TRIG, A3.GPIO14
  N2: A1.ECHO, A3.GPIO15
  GND: A1.GND, A2.GND, M1.Pin_4, A4.Pin_6, A5.Pin_6
  N3: A2.TRIG, A3.GPIO17
  N4: A2.ECHO, A3.GPIO27
  N5: L298N1.OUT1, DC_Mot_Enc1.pin6
  N6: L298N1.OUT2, DC_Mot_Enc1.pin5
  N7: L298N1.OUT3, DC_Mot_Enc2.pin5
  N8: L298N1.OUT4, DC_Mot_Enc2.pin6
  N9: L298N1.GND, DC_Mot_Enc1.pin2, DC_Mot_Enc2.pin2
  N10: L298N1.5V, DC_Mot_Enc1.pin1, DC_Mot_Enc2.pin1
  N11: L298N1.ENA, U1.GPIO25
  N12: L298N1.IN1, U1.GPIO26
  N13: L298N1.IN2, U1.GPIO27
  N14: DC_Mot_Enc1.pin3, DC_Mot_Enc2.pin3, U1.GPIO34
  N15: DC_Mot_Enc1.pin4, DC_Mot_Enc2.pin4, U1.GPIO35
  N16: Load_Cell1.wire1, A4.Pin_1
  N17: Load_Cell1.wire2, A4.Pin_3
  N18: Load_Cell1.wire3, A4.Pin_2
  N19: Load_Cell1.wire4, A4.Pin_4
  N20: Load_Cell2.wire1, A5.Pin_1
  N21: Load_Cell2.wire2, A5.Pin_3
  N22: Load_Cell2.wire3, A5.Pin_2
  N23: Load_Cell2.wire4, A5.Pin_4
  N24: A3.5V, M3.Pin_3
  N25: A3.GND, M3.Pin_4, A6.pin4
  N26: A3.GPIO23, A6.pin1
  N27: A3.GPIO24, A6.pin2
  N28: A3.GPIO25, A6.pin3
  N29: U1.GPIO32, J2.pulse
  N30: U1.GPIO33, J1.pulse
  N31: U1.GPIO18, A4.Pin_8
  N32: U1.GPIO19, A4.Pin_7
  N33: U1.GPIO22, A5.Pin_7
  N34: U1.GPIO23, A5.Pin_8
  GND_2: J1.gnd, J2.gnd, M2.Pin_4
  VCC_2: J1.vcc, J2.vcc, M2.Pin_3
  N35: S1.leg0, BAT3.-, M1.Pin_2, M2.Pin_2, M3.Pin_2, S2.leg0
  N36: S1.leg1, BAT3.+, M1.Pin_1, M2.Pin_1, M3.Pin_1, S2.leg1

notes:
  Left Motor
  Right Motor
  emergency stop button
  act like pcb

custom parts:
  HC-SR04 Ultrasonic Distance Sensor: The HC-SR04 is an ultrasonic distance sensor. It is capable of providing measurement for ranges of 2cm to 400cm. The module operates at 5V.
  L298N DC motor driver: 2x DC motor driver with 78M05 positive voltage regulator (7..35 V) L298N: max 46 V, 2 A Set 5 V Enable jumper to enable 5 V regultor (needed for the L298N) and +5 V output at screw terminal or supply external +5 V at screw terminal Set ENA and/or ENB to +5 V to enable motor permanently or supply ENA and/or ENB with PWM signal IN1 and IN2 set rotation directory for motor A (OUT1/OUT2) IN2 and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
  Load Cell - Red/white/black/green: A rectangle load cell/weighting pressure Sensor with four wires - Red, white, black, green. Normally corresponding with E+, E-, A+, A- respectively.
  Raspberry Pi 5: The RPi5, a faster version of the awesome Raspberry Pi4B ARM Board with 40 pin gpio.
  ESP32-38PinWide: Generic 38-Pin ESP32 with wide format (only access to one side of pins on a breadboard) based on Stephen Lilley's HiLetgo ESP-WROOM-32 ESP32 ESP-32S Development Board.
  12 battery: 12V lead acid type battery, like the Husqvarna YTH2448 12V 35AH battery. The pads in pcb are sized to accomidate up to 14ga wire (as these batterys will deliver high currents.)
  Sparkfun load cell amplifier: The SparkFun Load Cell Amplifier is a small breakout board for the HX711 IC that allows you to easily read load cells to measure weight.
  BBAA100043: BBAA100043 traffic light module.
